// Logisim project Lista2.circ as structural Verilog: 12 circuits, main circuit main
module main (
  input  Ci,
  input  A0,
  input  A1,
  input  A2,
  input  A3,
  input  B0,
  input  B1,
  input  B2,
  input  B3,
  output S0,
  output S1,
  output S2,
  output S3,
  output cO,
  output Overflow
);

  wire decodificador_hexa_1_a, decodificador_hexa_1_b, decodificador_hexa_1_c, decodificador_hexa_1_d,
       decodificador_hexa_1_e, decodificador_hexa_1_f, decodificador_hexa_1_g, decodificador_hexa_2_a,
       decodificador_hexa_2_b, decodificador_hexa_2_c, decodificador_hexa_2_d, decodificador_hexa_2_e,
       decodificador_hexa_2_f, decodificador_hexa_2_g, decodificador_hexa_3_a, decodificador_hexa_3_b,
       decodificador_hexa_3_c, decodificador_hexa_3_d, decodificador_hexa_3_e, decodificador_hexa_3_f,
       decodificador_hexa_3_g, decodificador_hexa_negativo_1_a, decodificador_hexa_negativo_1_b,
       decodificador_hexa_negativo_1_c, decodificador_hexa_negativo_1_d, decodificador_hexa_negativo_1_e,
       decodificador_hexa_negativo_1_f, decodificador_hexa_negativo_1_g, decodificador_hexa_negativo_1_h,
       decodificador_hexa_negativo_2_a, decodificador_hexa_negativo_2_b, decodificador_hexa_negativo_2_c,
       decodificador_hexa_negativo_2_d, decodificador_hexa_negativo_2_e, decodificador_hexa_negativo_2_f,
       decodificador_hexa_negativo_2_g, decodificador_hexa_negativo_2_h, decodificador_hexa_negativo_3_a,
       decodificador_hexa_negativo_3_b, decodificador_hexa_negativo_3_c, decodificador_hexa_negativo_3_d,
       decodificador_hexa_negativo_3_e, decodificador_hexa_negativo_3_f, decodificador_hexa_negativo_3_g,
       decodificador_hexa_negativo_3_h;

  Decodificador_Hexa decodificador_hexa_1 (
    .X3(A3), .X2(A2), .X1(A1), .a(decodificador_hexa_1_a), .X0(A0), .b(decodificador_hexa_1_b),
    .c(decodificador_hexa_1_c), .d(decodificador_hexa_1_d), .e(decodificador_hexa_1_e),
    .f(decodificador_hexa_1_f), .g(decodificador_hexa_1_g));
  Somador_de_4_bits somador_de_4_bits_1 (
    .Carry_In(Ci), .X0(A0), .X1(A1), .X2(A2), .S0(S0), .X3(A3), .S1(S1), .S2(S2), .Y0(B0), .S3(S3), .Y1(B1),
    .Carry_Out(cO), .Y2(B2), .Y3(B3), .Overflow(Overflow));
  Decodificador_Hexa decodificador_hexa_2 (
    .X3(B3), .X2(B2), .X1(B1), .a(decodificador_hexa_2_a), .X0(B0), .b(decodificador_hexa_2_b),
    .c(decodificador_hexa_2_c), .d(decodificador_hexa_2_d), .e(decodificador_hexa_2_e),
    .f(decodificador_hexa_2_f), .g(decodificador_hexa_2_g));
  _7_Segment_Display u_7_segment_display_1 (
    .g(decodificador_hexa_1_g), .f(decodificador_hexa_1_f), .a(decodificador_hexa_1_a),
    .b(decodificador_hexa_1_b), .e(decodificador_hexa_1_e), .d(decodificador_hexa_1_d),
    .c(decodificador_hexa_1_c), .dp(1'b0));
  _7_Segment_Display u_7_segment_display_2 (
    .g(decodificador_hexa_2_g), .f(decodificador_hexa_2_f), .a(decodificador_hexa_2_a),
    .b(decodificador_hexa_2_b), .e(decodificador_hexa_2_e), .d(decodificador_hexa_2_d),
    .c(decodificador_hexa_2_c), .dp(1'b0));
  Decodificador_Hexa_Negativo decodificador_hexa_negativo_1 (
    .X3(A3), .X2(A2), .X1(A1), .X0(A0), .a(decodificador_hexa_negativo_1_a),
    .b(decodificador_hexa_negativo_1_b), .c(decodificador_hexa_negativo_1_c),
    .d(decodificador_hexa_negativo_1_d), .e(decodificador_hexa_negativo_1_e),
    .f(decodificador_hexa_negativo_1_f), .g(decodificador_hexa_negativo_1_g),
    .h(decodificador_hexa_negativo_1_h));
  Decodificador_Hexa decodificador_hexa_3 (
    .X3(S3), .X2(S2), .X1(S1), .a(decodificador_hexa_3_a), .X0(S0), .b(decodificador_hexa_3_b),
    .c(decodificador_hexa_3_c), .d(decodificador_hexa_3_d), .e(decodificador_hexa_3_e),
    .f(decodificador_hexa_3_f), .g(decodificador_hexa_3_g));
  Decodificador_Hexa_Negativo decodificador_hexa_negativo_2 (
    .X3(B3), .X2(B2), .X1(B1), .X0(B0), .a(decodificador_hexa_negativo_2_a),
    .b(decodificador_hexa_negativo_2_b), .c(decodificador_hexa_negativo_2_c),
    .d(decodificador_hexa_negativo_2_d), .e(decodificador_hexa_negativo_2_e),
    .f(decodificador_hexa_negativo_2_f), .g(decodificador_hexa_negativo_2_g),
    .h(decodificador_hexa_negativo_2_h));
  _7_Segment_Display u_7_segment_display_3 (
    .g(decodificador_hexa_3_g), .f(decodificador_hexa_3_f), .a(decodificador_hexa_3_a),
    .b(decodificador_hexa_3_b), .e(decodificador_hexa_3_e), .d(decodificador_hexa_3_d),
    .c(decodificador_hexa_3_c), .dp(1'b0));
  _7_Segment_Display u_7_segment_display_4 (
    .g(decodificador_hexa_negativo_1_g), .f(decodificador_hexa_negativo_1_f),
    .a(decodificador_hexa_negativo_1_a), .b(decodificador_hexa_negativo_1_b),
    .e(decodificador_hexa_negativo_1_e), .d(decodificador_hexa_negativo_1_d),
    .c(decodificador_hexa_negativo_1_c), .dp(decodificador_hexa_negativo_1_h));
  _7_Segment_Display u_7_segment_display_5 (
    .g(decodificador_hexa_negativo_2_g), .f(decodificador_hexa_negativo_2_f),
    .a(decodificador_hexa_negativo_2_a), .b(decodificador_hexa_negativo_2_b),
    .e(decodificador_hexa_negativo_2_e), .d(decodificador_hexa_negativo_2_d),
    .c(decodificador_hexa_negativo_2_c), .dp(decodificador_hexa_negativo_2_h));
  Decodificador_Hexa_Negativo decodificador_hexa_negativo_3 (
    .X3(S3), .X2(S2), .X1(S1), .X0(S0), .a(decodificador_hexa_negativo_3_a),
    .b(decodificador_hexa_negativo_3_b), .c(decodificador_hexa_negativo_3_c),
    .d(decodificador_hexa_negativo_3_d), .e(decodificador_hexa_negativo_3_e),
    .f(decodificador_hexa_negativo_3_f), .g(decodificador_hexa_negativo_3_g),
    .h(decodificador_hexa_negativo_3_h));
  _7_Segment_Display u_7_segment_display_6 (
    .g(decodificador_hexa_negativo_3_g), .f(decodificador_hexa_negativo_3_f),
    .a(decodificador_hexa_negativo_3_a), .b(decodificador_hexa_negativo_3_b),
    .e(decodificador_hexa_negativo_3_e), .d(decodificador_hexa_negativo_3_d),
    .c(decodificador_hexa_negativo_3_c), .dp(decodificador_hexa_negativo_3_h));
endmodule

module Meio_Somador (
  input  A0,
  input  B0,
  output Soma,
  output Carry_Out
);

  xor xor_1 (Soma, A0, B0);
  and and_1 (Carry_Out, A0, B0);
endmodule

module Somador_Completo (
  input  X0,
  input  Y0,
  input  Carry_In,
  output S0,
  output Carry_Out
);

  wire meio_somador_1_carry_out, meio_somador_1_soma, meio_somador_2_carry_out;

  Meio_Somador meio_somador_1 (.Soma(meio_somador_1_soma), .Carry_Out(meio_somador_1_carry_out), .A0(X0), .B0(Y0));
  Meio_Somador meio_somador_2 (
    .Soma(S0), .Carry_Out(meio_somador_2_carry_out), .A0(meio_somador_1_soma), .B0(Carry_In));
  or or_1 (Carry_Out, meio_somador_2_carry_out, meio_somador_1_carry_out);
endmodule

module Somador_de_4_bits (
  input  Carry_In,
  input  X0,
  input  X1,
  input  X2,
  input  X3,
  input  Y0,
  input  Y1,
  input  Y2,
  input  Y3,
  output S0,
  output S1,
  output S2,
  output S3,
  output Overflow,
  output Carry_Out
);

  wire somador_completo_1_carry_out, somador_completo_2_carry_out, somador_completo_3_carry_out;

  Somador_Completo somador_completo_1 (
    .S0(S0), .Carry_Out(somador_completo_1_carry_out), .X0(X0), .Y0(Y0), .Carry_In(Carry_In));
  Somador_Completo somador_completo_2 (
    .S0(S1), .Carry_Out(somador_completo_2_carry_out), .X0(X1), .Y0(Y1),
    .Carry_In(somador_completo_1_carry_out));
  Somador_Completo somador_completo_3 (
    .S0(S2), .Carry_Out(somador_completo_3_carry_out), .X0(X2), .Y0(Y2),
    .Carry_In(somador_completo_2_carry_out));
  Somador_Completo somador_completo_4 (
    .S0(S3), .Carry_Out(Carry_Out), .X0(X3), .Y0(Y3), .Carry_In(somador_completo_3_carry_out));
  xor xor_1 (Overflow, somador_completo_3_carry_out, Carry_Out);
endmodule

module ULA_de_1_bit (
  input  Carry_In,
  input  a,
  input  b,
  input  b_invert,
  input  op1,
  input  op0,
  output S,
  output Carry_Out
);

  wire and_1_out, multiplexer_1_out, not_1_out, not_2_out, or_1_out, somador_de_1_bit_simplificado_1_s;

  not not_1 (not_1_out, b);
  not not_2 (not_2_out, a);
  Somador_de_1_bit___Simplificado somador_de_1_bit_simplificado_1 (
    .X(a), .Y(multiplexer_1_out), .Carry_In(Carry_In), .S(somador_de_1_bit_simplificado_1_s),
    .Carry_Out(Carry_Out));
  Multiplexer #(.enable("false")) multiplexer_1 (.in0(b), .in1(not_1_out), .out(multiplexer_1_out), .sel(b_invert));
  and and_1 (and_1_out, a, b);
  or or_1 (or_1_out, a, b);
  Multiplexer #(.select(2), .disabled(0), .enable("false")) multiplexer_2 (
    .in0(and_1_out), .in1(or_1_out), .in2(not_2_out), .in3(somador_de_1_bit_simplificado_1_s), .out(S),
    .sel({op1, op0}));
endmodule

module ULA_de_4_bits (
  input  B3,
  input  B2,
  input  B1,
  input  B0,
  input  A3,
  input  A2,
  input  A1,
  input  A0,
  input  Binvert,
  input  op1,
  input  op0,
  output S3,
  output S2,
  output S1,
  output S0,
  output Overflow,
  output Carry_Out
);

  wire ula_de_1_bit_1_carry_out, ula_de_1_bit_2_carry_out, ula_de_1_bit_3_carry_out;

  ULA_de_1_bit ula_de_1_bit_1 (
    .a(A0), .b(B0), .S(S0), .Carry_In(Binvert), .op1(op1), .op0(op0), .Carry_Out(ula_de_1_bit_1_carry_out),
    .b_invert(Binvert));
  ULA_de_1_bit ula_de_1_bit_2 (
    .a(A1), .b(B1), .S(S1), .Carry_In(ula_de_1_bit_1_carry_out), .op1(op1), .op0(op0),
    .Carry_Out(ula_de_1_bit_2_carry_out), .b_invert(Binvert));
  ULA_de_1_bit ula_de_1_bit_3 (
    .a(A2), .b(B2), .S(S2), .Carry_In(ula_de_1_bit_2_carry_out), .op1(op1), .op0(op0),
    .Carry_Out(ula_de_1_bit_3_carry_out), .b_invert(Binvert));
  ULA_de_1_bit ula_de_1_bit_4 (
    .a(A3), .b(B3), .S(S3), .Carry_In(ula_de_1_bit_3_carry_out), .op1(op1), .op0(op0), .Carry_Out(Carry_Out),
    .b_invert(Binvert));
  xor xor_1 (Overflow, ula_de_1_bit_3_carry_out, Carry_Out);

  // Other names for the same wires on the sheet: Bin = Binvert
endmodule

module ULA_de_4_bits___Completa (
  input  B3,
  input  B2,
  input  B1,
  input  B0,
  input  A3,
  input  A2,
  input  A1,
  input  A0,
  input  Binvert,
  input  op1,
  input  op0,
  output S3,
  output S2,
  output S1,
  output S0,
  output Flag_Zero,
  output Overflow,
  output Carry_Out
);

  wire ula_de_1_bit_1_carry_out, ula_de_1_bit_2_carry_out, ula_de_1_bit_3_carry_out;

  ULA_de_1_bit ula_de_1_bit_1 (
    .a(A0), .b(B0), .S(S0), .Carry_In(Binvert), .op1(op1), .op0(op0), .Carry_Out(ula_de_1_bit_1_carry_out),
    .b_invert(Binvert));
  ULA_de_1_bit ula_de_1_bit_2 (
    .a(A1), .b(B1), .S(S1), .Carry_In(ula_de_1_bit_1_carry_out), .op1(op1), .op0(op0),
    .Carry_Out(ula_de_1_bit_2_carry_out), .b_invert(Binvert));
  ULA_de_1_bit ula_de_1_bit_3 (
    .a(A2), .b(B2), .S(S2), .Carry_In(ula_de_1_bit_2_carry_out), .op1(op1), .op0(op0),
    .Carry_Out(ula_de_1_bit_3_carry_out), .b_invert(Binvert));
  ULA_de_1_bit ula_de_1_bit_4 (
    .a(A3), .b(B3), .S(S3), .Carry_In(ula_de_1_bit_3_carry_out), .op1(op1), .op0(op0), .Carry_Out(Carry_Out),
    .b_invert(Binvert));
  nand nand_1 (Flag_Zero, S0, S1, S2, S3);
  xor xor_1 (Overflow, ula_de_1_bit_3_carry_out, Carry_Out);

  // Other names for the same wires on the sheet: Bin = Binvert
endmodule

module Calculadora_de_4_bits (
  input  Ci,
  input  A0,
  input  A1,
  input  A2,
  input  A3,
  input  B0,
  input  B1,
  input  B2,
  input  B3,
  output S0,
  output S1,
  output S2,
  output S3,
  output cO,
  output Overflow
);

  wire decodificador_hexa_1_a, decodificador_hexa_1_b, decodificador_hexa_1_c, decodificador_hexa_1_d,
       decodificador_hexa_1_e, decodificador_hexa_1_f, decodificador_hexa_1_g, decodificador_hexa_2_a,
       decodificador_hexa_2_b, decodificador_hexa_2_c, decodificador_hexa_2_d, decodificador_hexa_2_e,
       decodificador_hexa_2_f, decodificador_hexa_2_g, decodificador_hexa_3_a, decodificador_hexa_3_b,
       decodificador_hexa_3_c, decodificador_hexa_3_d, decodificador_hexa_3_e, decodificador_hexa_3_f,
       decodificador_hexa_3_g;

  Decodificador_Hexa decodificador_hexa_1 (
    .X3(A3), .X2(A2), .X1(A1), .a(decodificador_hexa_1_a), .X0(A0), .b(decodificador_hexa_1_b),
    .c(decodificador_hexa_1_c), .d(decodificador_hexa_1_d), .e(decodificador_hexa_1_e),
    .f(decodificador_hexa_1_f), .g(decodificador_hexa_1_g));
  Somador_de_4_bits somador_de_4_bits_1 (
    .Carry_In(Ci), .X0(A0), .X1(A1), .X2(A2), .S0(S0), .X3(A3), .S1(S1), .S2(S2), .Y0(B0), .S3(S3), .Y1(B1),
    .Carry_Out(cO), .Y2(B2), .Y3(B3), .Overflow(Overflow));
  Decodificador_Hexa decodificador_hexa_2 (
    .X3(B3), .X2(B2), .X1(B1), .a(decodificador_hexa_2_a), .X0(B0), .b(decodificador_hexa_2_b),
    .c(decodificador_hexa_2_c), .d(decodificador_hexa_2_d), .e(decodificador_hexa_2_e),
    .f(decodificador_hexa_2_f), .g(decodificador_hexa_2_g));
  _7_Segment_Display u_7_segment_display_1 (
    .g(decodificador_hexa_1_g), .f(decodificador_hexa_1_f), .a(decodificador_hexa_1_a),
    .b(decodificador_hexa_1_b), .e(decodificador_hexa_1_e), .d(decodificador_hexa_1_d),
    .c(decodificador_hexa_1_c), .dp(1'b0));
  _7_Segment_Display u_7_segment_display_2 (
    .g(decodificador_hexa_2_g), .f(decodificador_hexa_2_f), .a(decodificador_hexa_2_a),
    .b(decodificador_hexa_2_b), .e(decodificador_hexa_2_e), .d(decodificador_hexa_2_d),
    .c(decodificador_hexa_2_c), .dp(1'b0));
  Decodificador_Hexa decodificador_hexa_3 (
    .X3(S3), .X2(S2), .X1(S1), .a(decodificador_hexa_3_a), .X0(S0), .b(decodificador_hexa_3_b),
    .c(decodificador_hexa_3_c), .d(decodificador_hexa_3_d), .e(decodificador_hexa_3_e),
    .f(decodificador_hexa_3_f), .g(decodificador_hexa_3_g));
  _7_Segment_Display u_7_segment_display_3 (
    .g(decodificador_hexa_3_g), .f(decodificador_hexa_3_f), .a(decodificador_hexa_3_a),
    .b(decodificador_hexa_3_b), .e(decodificador_hexa_3_e), .d(decodificador_hexa_3_d),
    .c(decodificador_hexa_3_c), .dp(1'b0));
endmodule

module Somador_de_1_bit___Simplificado (
  input  X,
  input  Y,
  input  Carry_In,
  output S,
  output Carry_Out
);

  Somador_Completo somador_completo_1 (.S0(S), .Carry_Out(Carry_Out), .X0(X), .Y0(Y), .Carry_In(Carry_In));
endmodule

module Somador_de_4_bits___Simplificado (
  input  [3:0] X,
  input  Carry_In,
  input  [3:0] Y,
  output [3:0] S,
  output Overflow,
  output Carry_Out
);

  Somador_de_4_bits somador_de_4_bits_1 (
    .Carry_In(Carry_In), .X0(X[0]), .X1(X[1]), .X2(X[2]), .S0(S[0]), .X3(X[3]), .S1(S[1]), .S2(S[2]),
    .Y0(Y[0]), .S3(S[3]), .Y1(Y[1]), .Carry_Out(Carry_Out), .Y2(Y[2]), .Y3(Y[3]), .Overflow(Overflow));
endmodule

module Decodificador_Hexa (
  input  X3,
  input  X2,
  input  X1,
  input  X0,
  output a,
  output b,
  output c,
  output d,
  output e,
  output f,
  output g
);

  wire and_1_out, and_2_out, and_3_out, and_4_out, and_5_out, and_6_out, and_7_out, and_8_out, and_9_out,
       and_10_out, and_11_out, and_12_out, and_13_out, and_14_out, and_15_out, and_16_out, and_17_out,
       and_18_out, and_19_out, and_20_out, and_21_out, and_22_out, and_23_out, and_24_out, and_25_out,
       and_26_out, and_27_out, and_28_out, and_29_out, and_30_out, and_31_out, and_32_out, and_33_out,
       and_34_out, and_35_out, and_36_out, and_37_out, and_38_out, and_39_out, and_40_out, and_41_out,
       and_42_out, and_43_out, and_44_out, not_1_out, not_2_out, not_3_out, not_4_out, not_5_out, not_6_out,
       not_7_out, not_8_out, not_9_out, not_10_out, not_11_out, not_12_out, not_13_out, not_14_out,
       not_15_out, not_16_out, not_17_out, not_18_out, not_19_out, not_20_out, not_21_out, not_22_out,
       not_23_out, not_24_out, not_25_out, not_26_out, not_27_out, not_28_out, not_29_out, not_30_out,
       not_31_out, not_32_out, not_33_out, not_34_out, not_35_out, not_36_out, not_37_out, not_38_out,
       not_39_out, not_40_out, not_41_out, not_42_out, or_1_out, or_2_out, or_3_out, or_4_out, or_5_out,
       or_6_out, or_7_out, or_8_out, or_9_out, or_10_out, or_11_out, or_12_out, or_14_out, or_17_out,
       or_18_out, or_20_out, or_21_out, or_22_out, or_23_out;

  not not_1 (not_1_out, X2);
  and and_1 (and_1_out, not_1_out, not_2_out);
  not not_2 (not_2_out, X0);
  not not_3 (not_3_out, X3);
  and and_2 (and_2_out, not_3_out, X1);
  not not_4 (not_4_out, X3);
  and and_3 (and_3_out, not_4_out, X2);
  and and_4 (and_4_out, X3, not_5_out);
  not not_5 (not_5_out, X2);
  not not_6 (not_6_out, X1);
  not not_7 (not_7_out, X3);
  not not_8 (not_8_out, X2);
  not not_9 (not_9_out, X3);
  and and_5 (and_5_out, not_9_out, not_10_out);
  not not_10 (not_10_out, X1);
  not not_11 (not_11_out, X0);
  not not_12 (not_12_out, X3);
  not not_13 (not_13_out, X1);
  not not_14 (not_14_out, X3);
  and and_6 (and_6_out, not_14_out, not_15_out);
  not not_15 (not_15_out, X1);
  not not_16 (not_16_out, X3);
  and and_7 (and_7_out, not_16_out, X0);
  not not_17 (not_17_out, X1);
  not not_18 (not_18_out, X3);
  not not_19 (not_19_out, X2);
  not not_20 (not_20_out, X3);
  and and_8 (and_8_out, not_20_out, not_21_out);
  not not_21 (not_21_out, X2);
  not not_22 (not_22_out, X0);
  not not_23 (not_23_out, X2);
  and and_9 (and_9_out, not_23_out, X1);
  not not_24 (not_24_out, X1);
  not not_25 (not_25_out, X2);
  and and_10 (and_10_out, not_25_out, not_26_out);
  not not_26 (not_26_out, X0);
  and and_11 (and_11_out, X1, not_27_out);
  not not_27 (not_27_out, X0);
  and and_12 (and_12_out, X3, X1);
  and and_13 (and_13_out, X3, X2);
  not not_28 (not_28_out, X3);
  and and_14 (and_14_out, not_28_out, not_29_out);
  not not_29 (not_29_out, X1);
  not not_30 (not_30_out, X0);
  not not_31 (not_31_out, X3);
  and and_15 (and_15_out, not_31_out, X2);
  not not_32 (not_32_out, X1);
  not not_33 (not_33_out, X3);
  not not_34 (not_34_out, X2);
  and and_16 (and_16_out, not_34_out, X1);
  and and_17 (and_17_out, X2, not_35_out);
  not not_35 (not_35_out, X1);
  and and_18 (and_18_out, X2, not_36_out);
  not not_36 (not_36_out, X0);
  or or_1 (or_1_out, and_1_out, and_2_out);
  and and_19 (and_19_out, and_3_out, X0);
  and and_20 (and_20_out, X2, X1);
  and and_21 (and_21_out, and_4_out, not_6_out);
  and and_22 (and_22_out, not_7_out, not_8_out);
  and and_23 (and_23_out, and_5_out, not_11_out);
  not not_37 (not_37_out, X2);
  not not_38 (not_38_out, X0);
  and and_24 (and_24_out, not_12_out, X1);
  and and_25 (and_25_out, X3, not_13_out);
  or or_2 (or_2_out, and_6_out, and_7_out);
  and and_26 (and_26_out, not_17_out, X0);
  and and_27 (and_27_out, not_18_out, X2);
  and and_28 (and_28_out, X3, not_19_out);
  and and_29 (and_29_out, and_8_out, not_22_out);
  and and_30 (and_30_out, and_9_out, X0);
  and and_31 (and_31_out, X2, not_24_out);
  and and_32 (and_32_out, X2, X1);
  not not_39 (not_39_out, X0);
  not not_40 (not_40_out, X1);
  or or_3 (or_3_out, and_10_out, and_11_out);
  or or_4 (or_4_out, and_12_out, and_13_out);
  and and_33 (and_33_out, and_14_out, not_30_out);
  and and_34 (and_34_out, and_15_out, not_32_out);
  and and_35 (and_35_out, not_33_out, X2);
  not not_41 (not_41_out, X0);
  not not_42 (not_42_out, X2);
  or or_5 (or_5_out, and_16_out, and_17_out);
  or or_6 (or_6_out, and_18_out, X3);
  or or_7 (or_7_out, or_1_out, and_19_out);
  or or_8 (or_8_out, and_20_out, and_21_out);
  or or_9 (or_9_out, and_22_out, and_23_out);
  and and_36 (and_36_out, not_37_out, not_38_out);
  and and_37 (and_37_out, and_24_out, X0);
  and and_38 (and_38_out, and_25_out, X0);
  or or_10 (or_10_out, or_2_out, and_26_out);
  or or_11 (or_11_out, and_27_out, and_28_out);
  or or_12 (or_12_out, and_29_out, and_30_out);
  and and_39 (and_39_out, and_31_out, X0);
  and and_40 (and_40_out, and_32_out, not_39_out);
  and and_41 (and_41_out, X3, not_40_out);
  or or_13 (e, or_3_out, or_4_out);
  or or_14 (or_14_out, and_33_out, and_34_out);
  and and_42 (and_42_out, and_35_out, not_41_out);
  and and_43 (and_43_out, X3, not_42_out);
  and and_44 (and_44_out, X3, X1);
  or or_15 (g, or_5_out, or_6_out);
  or or_16 (a, or_7_out, or_8_out);
  or or_17 (or_17_out, or_9_out, and_36_out);
  or or_18 (or_18_out, and_37_out, and_38_out);
  or or_19 (c, or_10_out, or_11_out);
  or or_20 (or_20_out, or_12_out, and_39_out);
  or or_21 (or_21_out, and_40_out, and_41_out);
  or or_22 (or_22_out, or_14_out, and_42_out);
  or or_23 (or_23_out, and_43_out, and_44_out);
  or or_24 (b, or_17_out, or_18_out);
  or or_25 (d, or_20_out, or_21_out);
  or or_26 (f, or_22_out, or_23_out);
endmodule

module Decodificador_Hexa_Negativo (
  input  X3,
  input  X2,
  input  X1,
  input  X0,
  output a,
  output b,
  output c,
  output d,
  output e,
  output f,
  output g,
  output h
);

  wire and_1_out, and_2_out, and_3_out, and_4_out, and_5_out, and_6_out, and_7_out, and_8_out, and_9_out,
       and_10_out, and_11_out, and_12_out, and_13_out, and_14_out, and_15_out, and_16_out, and_17_out,
       and_18_out, and_19_out, and_20_out, and_21_out, and_22_out, and_23_out, and_24_out, and_25_out,
       and_26_out, and_27_out, and_28_out, and_29_out, and_30_out, and_31_out, and_32_out, not_1_out,
       not_2_out, not_3_out, not_4_out, not_5_out, not_6_out, not_7_out, not_8_out, not_9_out, not_10_out,
       not_11_out, not_12_out, not_13_out, not_14_out, not_15_out, not_16_out, not_17_out, not_18_out,
       not_19_out, not_20_out, not_21_out, not_22_out, not_23_out, not_24_out, not_25_out, not_26_out,
       not_27_out, not_28_out, not_29_out, not_30_out, not_31_out, not_32_out, not_33_out, not_34_out,
       not_35_out, or_1_out, or_2_out, or_3_out, or_4_out, or_6_out, or_7_out, or_8_out, or_9_out, or_10_out,
       or_11_out, or_13_out, or_14_out, or_15_out, or_16_out;

  not not_1 (not_1_out, X2);
  and and_1 (and_1_out, not_1_out, not_2_out);
  not not_2 (not_2_out, X0);
  not not_3 (not_3_out, X3);
  and and_2 (and_2_out, not_3_out, X1);
  not not_4 (not_4_out, X0);
  and and_3 (and_3_out, X2, not_5_out);
  not not_5 (not_5_out, X1);
  not not_6 (not_6_out, X2);
  not not_7 (not_7_out, X3);
  and and_4 (and_4_out, not_7_out, not_8_out);
  not not_8 (not_8_out, X2);
  not not_9 (not_9_out, X2);
  and and_5 (and_5_out, not_9_out, not_10_out);
  not not_10 (not_10_out, X1);
  not not_11 (not_11_out, X1);
  not not_12 (not_12_out, X0);
  not not_13 (not_13_out, X3);
  and and_6 (and_6_out, not_13_out, X1);
  not not_14 (not_14_out, X1);
  not not_15 (not_15_out, X3);
  and and_7 (and_7_out, not_15_out, X2);
  and and_8 (and_8_out, X3, not_16_out);
  not not_16 (not_16_out, X2);
  not not_17 (not_17_out, X2);
  not not_18 (not_18_out, X0);
  not not_19 (not_19_out, X2);
  not not_20 (not_20_out, X0);
  and and_9 (and_9_out, X2, not_21_out);
  not not_21 (not_21_out, X1);
  not not_22 (not_22_out, X2);
  and and_10 (and_10_out, not_22_out, not_23_out);
  not not_23 (not_23_out, X0);
  and and_11 (and_11_out, X1, not_24_out);
  not not_24 (not_24_out, X0);
  not not_25 (not_25_out, X1);
  not not_26 (not_26_out, X0);
  not not_27 (not_27_out, X3);
  and and_12 (and_12_out, not_27_out, X2);
  not not_28 (not_28_out, X1);
  not not_29 (not_29_out, X3);
  and and_13 (and_13_out, not_29_out, X2);
  not not_30 (not_30_out, X0);
  and and_14 (and_14_out, X3, not_31_out);
  not not_31 (not_31_out, X2);
  not not_32 (not_32_out, X2);
  and and_15 (and_15_out, not_32_out, X1);
  and and_16 (and_16_out, X2, not_33_out);
  not not_33 (not_33_out, X1);
  and and_17 (and_17_out, X2, not_34_out);
  not not_34 (not_34_out, X0);
  and and_18 (and_18_out, X3, not_35_out);
  not not_35 (not_35_out, X0);
  or or_1 (or_1_out, and_1_out, and_2_out);
  and and_19 (and_19_out, X1, not_4_out);
  and and_20 (and_20_out, and_3_out, X0);
  and and_21 (and_21_out, X3, not_6_out);
  or or_2 (or_2_out, and_4_out, and_5_out);
  and and_22 (and_22_out, not_11_out, not_12_out);
  and and_23 (and_23_out, and_6_out, X0);
  and and_24 (and_24_out, X3, X2);
  or or_3 (or_3_out, not_14_out, X0);
  or or_4 (or_4_out, and_7_out, and_8_out);
  and and_25 (and_25_out, not_17_out, not_18_out);
  and and_26 (and_26_out, not_19_out, X1);
  and and_27 (and_27_out, X1, not_20_out);
  and and_28 (and_28_out, and_9_out, X0);
  or or_5 (e, and_10_out, and_11_out);
  and and_29 (and_29_out, not_25_out, not_26_out);
  and and_30 (and_30_out, and_12_out, not_28_out);
  and and_31 (and_31_out, and_13_out, not_30_out);
  and and_32 (and_32_out, and_14_out, X1);
  or or_6 (or_6_out, and_15_out, and_16_out);
  or or_7 (or_7_out, and_17_out, and_18_out);
  or or_8 (or_8_out, or_1_out, and_19_out);
  or or_9 (or_9_out, and_20_out, and_21_out);
  or or_10 (or_10_out, or_2_out, and_22_out);
  or or_11 (or_11_out, and_23_out, and_24_out);
  or or_12 (c, or_3_out, or_4_out);
  or or_13 (or_13_out, and_25_out, and_26_out);
  or or_14 (or_14_out, and_27_out, and_28_out);
  or or_15 (or_15_out, and_29_out, and_30_out);
  or or_16 (or_16_out, and_31_out, and_32_out);
  or or_17 (g, or_6_out, or_7_out);
  or or_18 (a, or_8_out, or_9_out);
  or or_19 (b, or_10_out, or_11_out);
  or or_20 (d, or_13_out, or_14_out);
  or or_21 (f, or_15_out, or_16_out);

  assign h = X3;
endmodule
